// Logisim project HALF_FULL_ADDER.circ as structural Verilog: 1 circuit, main circuit main
module main (
  input  A,
  input  B,
  input  A_2,
  input  B_2,
  input  C
);

  wire _7408_2_out, _7408_3_out, _7408_out, _7432_out, _7486_2_out, _7486_3_out, _7486_out;

  xor _7486 (_7486_out, A, B);
  LED led_1 (.in(_7486_out));
  LED led_2 (.in(_7408_out));
  and _7408 (_7408_out, B, A, A);
  xor _7486_2 (_7486_2_out, A_2, B_2);
  and _7408_2 (_7408_2_out, B_2, A_2);
  xor _7486_3 (_7486_3_out, _7486_2_out, C);
  and _7408_3 (_7408_3_out, C, _7486_2_out);
  LED led_3 (.in(_7486_3_out));
  or _7432 (_7432_out, _7408_3_out, _7408_2_out);
  LED led_4 (.in(_7432_out));

  // Notes on the sheet:
  //   SUM
  //   CARRY
  //   SUM
  //   CARRY
endmodule
