// Logisim project NAND GATE.circ as structural Verilog: 1 circuit, main circuit main
module main (
  input  A,
  input  A_2,
  input  B,
  input  A_3,
  input  B_2,
  input  A_4,
  input  A_5,
  input  B_3,
  input  B_4
);

  wire nand_1_out, nand_2_out, nand_3_out, nand_4_out, nand_5_out, nand_6_out, nand_7_out, nand_8_out,
       nand_9_out, nand_10_out, nand_11_out, nand_12_out, nand_13_out, nand_14_out;

  nand nand_1 (nand_1_out, A_3, B_2);
  nand nand_2 (nand_2_out, A_4, A_4);
  nand nand_3 (nand_3_out, B_4, B_4);
  nand nand_4 (nand_4_out, A, A);
  LED led_1 (.in(nand_4_out));
  nand nand_5 (nand_5_out, nand_1_out, nand_1_out);
  LED led_2 (.in(nand_5_out));
  LED led_3 (.in(nand_6_out));
  nand nand_6 (nand_6_out, nand_2_out, nand_3_out);
  nand nand_7 (nand_7_out, A_5, B_3);
  nand nand_8 (nand_8_out, A_2, A_2);
  nand nand_9 (nand_9_out, B, B);
  nand nand_10 (nand_10_out, nand_8_out, nand_9_out);
  nand nand_11 (nand_11_out, A_5, nand_7_out);
  nand nand_12 (nand_12_out, nand_7_out, B_3);
  not nand_13 (nand_13_out, nand_10_out);  // NAND_Gate
  nand nand_14 (nand_14_out, nand_11_out, nand_12_out);
  LED led_4 (.in(nand_13_out));
  LED led_5 (.in(nand_14_out));

  // Notes on the sheet:
  //   (a)NOT GATE
  //   (c)OR GATE
  //   (b)AND GATE
  //   Y=A.B
  //   Y=A'
  //   Y=A+B
  //   Y
  //   Y
  //   Y
  //   (d)NOR GATE
  //   (e)Ex-OR GATE
  //   Y=(A+B)'
  //   Y
  //   Y
endmodule
