// Logisim project NOR GATE (1).circ as structural Verilog: 1 circuit, main circuit main
module main (
  input  A,
  input  A_2,
  input  A_3,
  input  B,
  input  B_2,
  input  A_4,
  input  B_3,
  input  A_5,
  input  B_4
);

  wire nor_1_out, nor_2_out, nor_3_out, nor_4_out, nor_5_out, nor_6_out, nor_7_out, nor_8_out, nor_9_out,
       nor_10_out, nor_11_out, nor_12_out, nor_13_out, nor_14_out;

  nor nor_1 (nor_1_out, A, A);
  nor nor_2 (nor_2_out, A_3, A_3);
  nor nor_3 (nor_3_out, B_2, B_2);
  nor nor_4 (nor_4_out, A_4, B_3);
  nor nor_5 (nor_5_out, A_5, A_5);
  nor nor_6 (nor_6_out, B_4, B_4);
  LED led_1 (.in(nor_1_out));
  nor nor_7 (nor_7_out, nor_2_out, nor_3_out);
  nor nor_8 (nor_8_out, nor_4_out, nor_4_out);
  nor nor_9 (nor_9_out, nor_5_out, nor_6_out);
  LED led_2 (.in(nor_7_out));
  LED led_3 (.in(nor_8_out));
  LED led_4 (.in(nor_10_out));
  nor nor_10 (nor_10_out, nor_9_out, nor_9_out);
  nor nor_11 (nor_11_out, A_2, B);
  nor nor_12 (nor_12_out, A_2, nor_11_out);
  nor nor_13 (nor_13_out, nor_11_out, B);
  nor nor_14 (nor_14_out, nor_12_out, nor_13_out);
  LED led_5 (.in(nor_14_out));

  // Notes on the sheet:
  //   (a)NOT GATE
  //   (b)AND GATE
  //   (c)OR GATE
  //   (d)NAND GATE
  //   Y=A'
  //   Y=A+B
  //   Y
  //   Y=A.B
  //   Y=(AB)'
  //   Y
  //   Y
  //   (e)Ex-NOR GATE
  //   Y
  //   Y
endmodule
