// Logisim project LOGIC GATES.circ as structural Verilog: 1 circuit, main circuit main
module main (
  input  A,
  input  B,
  input  A_2,
  input  A_3,
  input  B_2
);

  wire and_1_out, not_1_out, or_1_out;

  and and_1 (and_1_out, A, B);
  not not_1 (not_1_out, A_2);
  or or_1 (or_1_out, A_3, B_2);
  LED led_1 (.in(and_1_out));
  LED led_2 (.in(not_1_out));
  LED led_3 (.in(or_1_out));

  // Notes on the sheet:
  //   AND GATE
  //   NOT GATE
  //   OR GATE
  //   Y
  //   Y
  //   Y
endmodule
